# Fritzing sketch dragonschema (saved by Fritzing 0.9.3b)
breadboards: 1

parts:
  Raspberry_Pi_1 = Raspberry Pi 3 [part_number=RPI-3-V1.2]
  LED1 = LED - 5mm [color="Red (633nm)" package="5 mm [THT]"]
  R1 = Resistor [tolerance=±5% resistance=220 package=THT]
  J1 = Cobbler Plus Cable
  VCC1 = Battery
  J2 = Basic Servo

nets:
  3V3: Raspberry_Pi_1.3v3, Raspberry_Pi_1.3V3, J1.3.3V#41, J1.3.3V#57
  N1: Raspberry_Pi_1.GPIO2, J1.GPIO_2
  N2: Raspberry_Pi_1.GPIO3, J1.GPIO_3
  N3: Raspberry_Pi_1.GPIO4, J1.GPIO_4
  N4: Raspberry_Pi_1.GND, J1.GND#46, J1.GND#49, J1.GND#54, J1.GND#60, J1.GND#65, J1.GND#70, J1.GND#74, J1.GND#79
  N5: Raspberry_Pi_1.GPIO17, J1.GPIO_17
  N6: Raspberry_Pi_1.GPIO27, J1.GPIO_27
  N7: Raspberry_Pi_1.GPIO22, J1.GPIO_22
  N8: Raspberry_Pi_1.GPIO10, J1.GPIO_10
  N9: Raspberry_Pi_1.GPIO9, J1.GPIO_9
  N10: Raspberry_Pi_1.GPIO11, J1.GPIO_11
  N11: Raspberry_Pi_1.ID_SD, J1.ID_SD
  N12: Raspberry_Pi_1.GPIO5, J1.GPIO_5
  N13: Raspberry_Pi_1.GPIO6, J1.GPIO_6
  N14: Raspberry_Pi_1.GPIO13, J1.GPIO_13
  N15: Raspberry_Pi_1.GPIO19, J1.GPIO_19
  N16: Raspberry_Pi_1.GPIO26, J1.GPIO_26
  N17: Raspberry_Pi_1.GPIO21, J1.GPIO_21
  N18: Raspberry_Pi_1.GPIO20, J1.GPIO_20
  N19: Raspberry_Pi_1.GPIO16, J1.GPIO_16
  N20: Raspberry_Pi_1.GPIO12, J1.GPIO_12
  N21: Raspberry_Pi_1.ID_SC, J1.ID_SC
  N22: Raspberry_Pi_1.GPIO7, J1.GPIO_7
  N23: Raspberry_Pi_1.GPIO8, J1.GPIO_8
  N24: Raspberry_Pi_1.GPIO25, J1.GPIO_25
  N25: Raspberry_Pi_1.GPIO24, J1.GPIO_24
  N26: Raspberry_Pi_1.GPIO23, J1.GPIO_23
  N27: Raspberry_Pi_1.GPIO18, J1.GPIO_18
  N28: Raspberry_Pi_1.GPIO15, J1.GPIO_15
  N29: Raspberry_Pi_1.GPIO14, J1.GPIO_14
  5V: Raspberry_Pi_1.5V, J1.5V
  N30: LED1.cathode, R1.Pin_1
  N31: LED1.anode, J1.#18
  N32: R1.Pin_0, J1.GND#13
  N33: J1.#22, J2.pulse
  N34: J1.GND#38, VCC1.-, J2.gnd

custom parts:
  Cobbler Plus Cable: The Cobbler Plus is an add on prototyping board from Adafruit specifically designed for the Raspberry Pi B+ that can break out all those tasty power, GPIO, I2C and SPI pins from the 40-pin header onto a solderless breadboard. This set will make "cobbling together" prototypes with the Pi super easy. The Cobbler Plus can plug into any solderless breadboard.
